# Fritzing sketch sketch_0 (saved by Fritzing 0.9.3b)

parts:
  WeMos_D1_Mini1 = WeMos D1 Mini
  S1 = Reed switch [package=THT]
  BATT1 = LiPoly Battery (1300mAh)

nets:
  N1: WeMos_D1_Mini1.5V, BATT1.positive
  N2: WeMos_D1_Mini1.D0, WeMos_D1_Mini1.RST, S1.pin_2
  N3: WeMos_D1_Mini1.G, S1.pin_1, BATT1.negative

custom parts:
  LiPoly Battery (1300mAh): Lithium Ion Polymer Battery (1300mAh)
