# Fritzing sketch sketch_1 (saved by Fritzing 0.9.3b)

parts:
  R2 = Resistor [tolerance=±5% resistance=100k package=THT]
  R3 = Resistor [tolerance=±5% resistance=100k package=THT]
  WeMos_D1_Mini1 = WeMos D1 Mini
  S1 = Reed switch [package=THT]
  Q1 = npn-Powertransistor [package="TO220 [THT]"]
  BATT1 = LiPoly Battery (1300mAh)

nets:
  N1: R2.Pin_0, R3.Pin_0, S1.pin_1, Q1.base
  N2: R2.Pin_1, WeMos_D1_Mini1.5V, BATT1.positive
  N3: R3.Pin_1, WeMos_D1_Mini1.G, S1.pin_2, Q1.emitter, BATT1.negative
  N4: WeMos_D1_Mini1.D0, WeMos_D1_Mini1.RST, Q1.collector

notes:
  Это нужно чтобы инвертировать геркон
  (This is needed to invert the reed switch)
  IFRZ44N
  1 - Затвор (Gate)
  2 - Сток (Drain)
  3 - Исток (Source)

custom parts:
  LiPoly Battery (1300mAh): Lithium Ion Polymer Battery (1300mAh)
