# Fritzing sketch sketch_2 (saved by Fritzing 0.9.3b)

parts:
  R1 = Resistor [tolerance=±5% resistance=100k package=THT]
  R3 = Resistor [tolerance=±5% resistance=100k package=THT]
  S1 = Reed switch [package=THT]
  Q1 = npn-Powertransistor [package="TO220 [THT]"]
  BATT1 = LiPoly Battery (1300mAh)
  R2 = Resistor [tolerance=±5% resistance=100k package=THT]
  WeMos_D1_Mini1 = WeMos D1 Mini

nets:
  N1: R1.Pin_0, R3.Pin_0, S1.pin_1, Q1.base
  N2: R1.Pin_1, BATT1.positive, R2.Pin_1, WeMos_D1_Mini1.5V
  N3: R3.Pin_1, S1.pin_2, Q1.emitter, BATT1.negative, WeMos_D1_Mini1.G
  N4: Q1.collector, WeMos_D1_Mini1.D0, WeMos_D1_Mini1.RST
  N5: R2.Pin_0, WeMos_D1_Mini1.A0

notes:
  Это нужно чтобы инвертировать геркон
  (This is needed to invert the reed switch)
  IFRZ44N
  1 - Затвор (Gate)
  2 - Сток (Drain)
  3 - Исток (Source)

custom parts:
  LiPoly Battery (1300mAh): Lithium Ion Polymer Battery (1300mAh)
