# Fritzing sketch sketch_full (saved by Fritzing 0.9.3b)

parts:
  R2 = Resistor [tolerance=±5% resistance=100k package=THT]
  R3 = Resistor [tolerance=±5% resistance=100k package=THT]
  WeMos_D1_Mini1 = WeMos D1 Mini
  R1 = Resistor [tolerance=±5% resistance=100k package=THT]
  S1 = Reed switch [package=THT]
  Q1 = npn-Powertransistor [package="TO220 [THT]"]
  J1 = female pin header, 7 pins [form="♀ (female)"]
  J2 = Piezo Speaker
  BATT1 = LiPoly Battery (1300mAh)
  TP1 = TP4056 [chip_label=TP4056 package="DIP (Dual Inline) [THT]"]

nets:
  N1: R2.Pin_0, R3.Pin_0, S1.pin_1, Q1.base
  N2: R2.Pin_1, WeMos_D1_Mini1.5V, R1.Pin_1, TP1.pin3
  N3: R3.Pin_1, WeMos_D1_Mini1.G, S1.pin_2, Q1.emitter, J1.pin6, J2.pin1, TP1.pin6
  N4: WeMos_D1_Mini1.3V3, J1.pin7
  N5: WeMos_D1_Mini1.A0, R1.Pin_0
  N6: WeMos_D1_Mini1.D0, WeMos_D1_Mini1.RST, Q1.collector
  N7: WeMos_D1_Mini1.D1, J2.pin2
  N8: WeMos_D1_Mini1.D2, J1.pin1
  N9: WeMos_D1_Mini1.D3, J1.pin5
  N10: WeMos_D1_Mini1.D5, J1.pin2
  N11: WeMos_D1_Mini1.D7, J1.pin4
  N12: WeMos_D1_Mini1.D8, J1.pin3
  N13: BATT1.positive, TP1.pin4
  N14: BATT1.negative, TP1.pin5

notes:
  Это нужно чтобы инвертировать геркон
  (This is needed to invert the reed switch)
  IFRZ44N
  1 - Затвор (Gate)
  2 - Сток (Drain)
  3 - Исток (Source)
  E-ink 1.54'
  1 - BUSY D2
  2 - CLK D5
  3 - CS D8
  4 - SDI D7
  5 - D\C D3
  6 - GND GND
  7 - VCC 3v3

custom parts:
  LiPoly Battery (1300mAh): Lithium Ion Polymer Battery (1300mAh)
  TP4056: A DIP stand-in part for whatever IC you want. With 6 pins on a 300mil dual inline package (DIP) footprint.
